// Logisim project Simple_8bit_ALU.circ as structural Verilog: 2 circuits, main circuit CPU_8BIT
module ALU_8BIT (
  input  [7:0] A,
  input  [7:0] B,
  input  [3:0] OPCODE,
  output [7:0] RESULT,
  output Z,
  output EQ,
  output LT,
  output GT
);

  wire CMP_EQ, CMP_GT, CMP_LT, IS_CMP;
  wire [7:0] D0, D1, D2, D4, D5, D6, D7, D8, D9, D10, D11, D12;

  Adder #(.width(8)) ADD (.a(A), .b(B), .out(D0), .cin(1'b0));  // open: cout
  Adder #(.width(8)) INC (.a(A), .b(8'h1), .out(D1), .cin(1'b0));  // open: cout
  Subtractor #(.width(8)) DEC (.a(A), .b(8'h1), .out(D2), .bin(1'b0));  // open: bout
  Comparator #(.width(8), .mode("unsigned")) CMP (.a(A), .b(B), .gt(CMP_GT), .eq(CMP_EQ), .lt(CMP_LT));
  assign D4 = ~A;  // NOT_Gate NOT, 8 bits wide
  assign D5 = A & B;  // AND_Gate AND, 8 bits wide
  assign D6 = A | B;  // OR_Gate OR, 8 bits wide
  Shifter #(.width(8), .shift("lr")) SHR (.in(A), .\dist (3'b001), .out(D7));
  Shifter #(.width(8), .shift("ll")) SHL (.in(A), .\dist (3'b001), .out(D8));
  Subtractor #(.width(8)) SUB (.a(A), .b(B), .out(D9), .bin(1'b0));  // open: bout
  // XOR_Gate #(.width(8)) XOR: pin names not known; wires that end beside it: A, B, D10
  // NAND_Gate #(.width(8)) NAND: pin names not known; wires that end beside it: A, B, D11
  // NOR_Gate #(.width(8)) NOR: pin names not known; wires that end beside it: A, B, D12
  Multiplexer #(.select(4), .width(8), .enable("false")) SELECT_16 (
    .in0(D0), .in1(D1), .in2(D2), .in3({8{1'b0}}), .in4(D4), .in5(D5), .in6(D6), .in7(D7), .in8(D8),
    .in9(D9), .in10(D10), .in11(D11), .in12(D12), .in13(A), .in14({8{1'b0}}), .in15({8{1'b0}}), .out(RESULT),
    .sel(OPCODE));
  Comparator #(.width(8), .mode("unsigned")) ZeroTest (.a(RESULT), .b({8{1'b0}}), .eq(Z));  // open: gt, lt
  Comparator #(.width(4), .mode("unsigned")) IsCMP (.a(OPCODE), .b(4'b0011), .eq(IS_CMP));  // open: gt, lt
  and u_EQ (EQ, CMP_EQ, IS_CMP);
  and u_LT (LT, CMP_LT, IS_CMP);
  and u_GT (GT, CMP_GT, IS_CMP);

  // Other names for the same wires on the sheet: D13[7:0] = A; RESULT_BUS[7:0] = RESULT

  // Notes on the sheet:
  //   8-BIT ALU  /  14 OPERATIONS  /  4-BIT OPCODE
  //   A and B unsigned 8-bit; outputs are 8-bit modulo 256. CMP result = 00.
  //   JZ (E) and JMP (F) are reserved only; no branch-control hardware here.
  //   Status flag generation
endmodule

module CPU_8BIT (
  input  [7:0] DATA_A,
  input  LOAD_A,
  input  [7:0] DATA_B,
  input  LOAD_B,
  input  [3:0] OPCODE,
  input  EXEC,
  input  CLK,
  input  RESET,
  output [7:0] A_BUS_OUT,
  output [7:0] B_BUS_OUT,
  output [7:0] R_BUS_OUT,
  output [7:0] ALU_RESULT_OUT,
  output Z_OUT,
  output EQ_OUT,
  output LT_OUT,
  output GT_OUT,
  output IS_VALID_OUT,
  output A_WRITE_EN_OUT
);

  wire EXEC_VALID, IS_CMP, NOT_CMP, NOT_LOAD_A, WB_ENABLE, WB_SELECT;
  wire [7:0] A_DATA_IN;

  Multiplexer #(.select(1), .width(8), .enable("false")) A_SOURCE (
    .in0(DATA_A), .in1(ALU_RESULT_OUT), .out(A_DATA_IN));  // open: sel
  Register #(.width(8), .trigger("rising")) REG_A (
    .D(A_DATA_IN), .en(A_WRITE_EN_OUT), .clk(CLK), .Q(A_BUS_OUT), .clr(RESET));
  Register #(.width(8), .trigger("rising")) REG_B (.D(DATA_B), .en(LOAD_B), .clk(CLK), .Q(B_BUS_OUT), .clr(RESET));
  Comparator #(.width(4), .mode("unsigned")) IS_VALID (.a(OPCODE), .b(4'b1110), .lt(IS_VALID_OUT));  // open: gt, eq
  Comparator #(.width(4), .mode("unsigned")) u_IS_CMP (.a(OPCODE), .b(4'b0011), .eq(IS_CMP));  // open: gt, lt
  not NON_CMP (NOT_CMP, IS_CMP);
  not u_NOT_LOAD_A (NOT_LOAD_A, LOAD_A);
  // ALU_8BIT ALU: pin names not known; wires that end beside it: A_BUS_OUT, B_BUS_OUT, OPCODE, ALU_RESULT_OUT, Z_OUT, EQ_OUT, LT_OUT, GT_OUT
  and u_EXEC_VALID (EXEC_VALID, EXEC, IS_VALID_OUT);
  and u_WB_ENABLE (WB_ENABLE, EXEC_VALID, NOT_CMP);
  or A_WRITE_EN (A_WRITE_EN_OUT, WB_ENABLE, LOAD_A);
  Register #(.width(8), .trigger("rising")) REG_R (
    .D(ALU_RESULT_OUT), .en(EXEC_VALID), .clk(CLK), .Q(R_BUS_OUT), .clr(RESET));
  and u_WB_SELECT (WB_SELECT, WB_ENABLE, NOT_LOAD_A);

  // Other names for the same wires on the sheet: A_BUS[7:0] = A_BUS_OUT; A_WRITE_EN = A_WRITE_EN_OUT;
  //   ALU_RESULT[7:0] = ALU_RESULT_OUT; B_BUS[7:0] = B_BUS_OUT; EQ = EQ_OUT; GT = GT_OUT; IS_VALID = IS_VALID_OUT;
  //   LT = LT_OUT; R_BUS[7:0] = R_BUS_OUT; Z = Z_OUT

  // Notes on the sheet:
  //   8-BIT CPU DATAPATH / REGISTER & CONTROL DEMONSTRATOR
  //   LOAD_A or LOAD_B + pulse CLK to load external data; select OPCODE then EXEC + pulse CLK for ALU step.
  //   For clear operation, hold RESET=0. Avoid asserting EXEC and LOAD_A at the same time.
  //   No PC, ROM, RAM, instruction fetch, or branch execution. JZ/JMP remain reserved.
  //   CONTROL: VALID, CMP detection, A write-enable and write-back selector
endmodule
